# Fritzing sketch csci3410_fritzing (saved by Fritzing 0.9.1b)
breadboards: 1

parts:
  Part1 = Arduino Uno (Rev3)
  R1 = Trimmer Potentiometer [maximum_resistance=10kΩ package=THT]
  LED1 = RGB LED (com. cathode, rgb) [package="5 mm [THT]"]

nets:
  N1: Part1.D9_PWM, LED1.green_anode
  N2: Part1.D10_PWM/SS, LED1.blue_anode
  N3: Part1.D11_PWM/MOSI, LED1.red_anode
  N4: Part1.GND, R1.wiper, LED1.common_cathode
